// Logisim project s-mips.circ as structural Verilog
module S_MIPS_Board (
  input  DESHABILITAR_DISPATCHER,
  output halt
);

  wire button_1_out, CLK, CS, d_ff_1_q, LCLR, LoadRAM, LoadRAMOn, LW, R_R_W, R_W, ram_dispatcher_1_finished,
       RCS, Reset_out, RST, TTY_EN;
  wire [2:0] KDB;
  wire [3:0] LMask, Mask, ram_1_read_time, ram_1_write_time, RMask;
  wire [6:0] KDB_DATA, TTY_DATA;
  wire [15:0] Addr, LAddr, RAddr;
  wire [31:0] I0, I1, I2, I3, LData, ram_1_data_out_0, ram_1_data_out_1, ram_1_data_out_2, ram_1_data_out_3,
       RI0, RI1, RI2, RI3;

  TTY #(.rows(25), .cols(80)) tty_1 (.data(TTY_DATA), .clk(CLK), .we(TTY_EN), .clr(RST));
  not not_1 (LoadRAMOn, ram_dispatcher_1_finished);
  RAM_Dispatcher ram_dispatcher_1 (
    .WriteTime(ram_1_write_time), .Clock(CLK), .Data(LData), .Address(LAddr), .Mask(LMask),
    .Finished(ram_dispatcher_1_finished), .Write(LW), .CLR(LCLR));
  Keyboard #(.buflen(64)) keyboard_1 (.clk(CLK), .re(KDB[0]), .avail(KDB[2]), .data(KDB_DATA));  // open: clr
  RAM ram_1 (
    .Address(RAddr), .Data_Out_0(ram_1_data_out_0), .Data_Out_1(ram_1_data_out_1),
    .Data_Out_2(ram_1_data_out_2), .Data_Out_3(ram_1_data_out_3), .Data_In_0(RI0), .Data_In_1(RI1),
    .Data_In_2(RI2), .Data_In_3(RI3), .Mask(RMask), .nRead_Write(R_R_W), .Chip_Select(RCS),
    .Read_Time(ram_1_read_time), .Reset(button_1_out), .Write_Time(ram_1_write_time));
  Button button_1 (.out(button_1_out));
  D_Flip_Flop d_ff_1 (.clk(CLK), .D(1'b1), .Q(d_ff_1_q), .reset(Reset_out));  // open: Qn, preset, en
  Button Reset (.out(Reset_out));
  S_MIPS s_mips_1 (
    .Kbd_Enable(KDB[0]), .Address(Addr), .Kbd_Clear(KDB[1]), .Kbd_Available(KDB[2]), .RAM_In_0(I0),
    .Kbd_ASCII_Data(KDB_DATA), .RAM_In_1(I1), .TTY_Enable(TTY_EN), .RAM_In_2(I2), .RAM_In_3(I2),
    .TTY_ASCII_Data(TTY_DATA), .Reset(RST), .RAM_Out_0(ram_1_data_out_0), .Clock(CLK),
    .RAM_Out_1(ram_1_data_out_1), .Stop(halt), .RAM_Out_2(ram_1_data_out_2), .RAM_Out_3(ram_1_data_out_3),
    .Mask(Mask), .Read_Time(ram_1_read_time), .Write_Time(ram_1_write_time), .nRead_Write(R_W),
    .Chip_Select(CS));
  D_Flip_Flop d_ff_2 (.clk(CLK), .D(d_ff_1_q), .Qn(LCLR), .reset(Reset_out));  // open: Q, preset, en
  or or_1 (RST, LCLR, LoadRAM);
  Clock clock_1 (.out(CLK));
  Multiplexer #(.width(32), .enable("false")) multiplexer_1 (.in0(I0), .in1(LData), .out(RI0), .sel(LoadRAM));
  Multiplexer #(.width(32), .enable("false")) multiplexer_2 (.in0(I1), .in1(LData), .out(RI1), .sel(LoadRAM));
  Multiplexer #(.width(32), .enable("false")) multiplexer_3 (.in0(I2), .in1(LData), .out(RI2), .sel(LoadRAM));
  Multiplexer #(.width(32), .enable("false")) multiplexer_4 (.in0(I3), .in1(LData), .out(RI3), .sel(LoadRAM));
  and and_1 (LoadRAM, ~DESHABILITAR_DISPATCHER, LoadRAMOn);  // AND_Gate
  Multiplexer #(.width(16), .enable("false")) multiplexer_5 (.in0(Addr), .in1(LAddr), .out(RAddr), .sel(LoadRAM));
  Multiplexer #(.width(4), .enable("false")) multiplexer_6 (.in0(Mask), .in1(LMask), .out(RMask), .sel(LoadRAM));
  Multiplexer #(.enable("false")) multiplexer_7 (.in0(CS), .in1(LW), .out(RCS), .sel(LoadRAM));
  Multiplexer #(.enable("false")) multiplexer_8 (.in0(R_W), .in1(LW), .out(R_R_W), .sel(LoadRAM));

  // Notes on the sheet:
  //   NO MODIFICAR
  //   Keyboard
endmodule

module RAM (
  input  [15:0] Address,
  input  [31:0] Data_In_0,
  input  [31:0] Data_In_1,
  input  [31:0] Data_In_2,
  input  [31:0] Data_In_3,
  input  [3:0] Mask,
  input  nRead_Write,
  input  Chip_Select,
  input  Reset,
  output [31:0] Data_Out_0,
  output [31:0] Data_Out_1,
  output [31:0] Data_Out_2,
  output [31:0] Data_Out_3,
  output [3:0] Read_Time,
  output [3:0] Write_Time
);

  wire and_2_out, and_3_out, and_4_out, and_5_out, and_6_out, and_7_out, and_8_out, and_9_out, Changed, CLK,
       comparator_2_eq, comparator_3_eq, comparator_4_eq, comparator_5_eq, comparator_6_eq, Count,
       demultiplexer_3_out0, Idle, Idle_q, Load, Load0, Load1, nand_1_out, or_1_out, or_2_out, or_3_out,
       or_4_out, or_5_out, or_6_out, or_7_out, or_8_out, or_9_out, or_10_out, Proc_q, Update_Mem, Zero_Time;
  wire [3:0] counter_1_q, multiplexer_1_out, subtractor_1_out;
  wire [31:0] register_1_q, register_2_q, register_3_q, register_4_q, register_5_q;

  // Probe on 4'b0011
  // Probe on 4'b0010
  Multiplexer #(.width(4), .enable("false")) multiplexer_1 (
    .in0(4'b0011), .in1(4'b0010), .out(multiplexer_1_out), .sel(nRead_Write));
  or or_1 (or_1_out, Idle, Update_Mem);
  or or_2 (or_2_out, ~Chip_Select, Reset);  // OR_Gate
  Subtractor #(.width(4)) subtractor_1 (.a(multiplexer_1_out), .b(4'b0010), .out(subtractor_1_out));  // open: bin, bout
  D_Flip_Flop u_Idle (.clk(CLK), .D(or_1_out), .Q(Idle_q), .preset(or_2_out));  // open: Qn, en, reset
  Demultiplexer #(.enable("false")) demultiplexer_1 (.out0(Idle), .out1(Load0), .in(Idle_q), .sel(Changed));
  // Probe on counter_1_q
  Counter #(.width(4), .max('hf)) counter_1 (
    .load(Load), .D(subtractor_1_out), .count(Count), .Q(counter_1_q), .clk(CLK), .clr(or_3_out));  // open: carry
  or or_3 (or_3_out, ~Chip_Select, Reset);  // OR_Gate
  Comparator #(.width(4), .mode("unsigned")) comparator_1 (
    .a(4'b0000), .b(counter_1_q), .eq(Zero_Time));  // open: gt, lt
  or or_4 (or_4_out, Count, Load0, Load1);
  Register #(.width(32)) register_1 (.D(Data_In_0), .en(Chip_Select), .Q(register_1_q), .clk(CLK), .clr(or_5_out));
  or or_5 (or_5_out, ~Chip_Select, Reset);  // OR_Gate
  Register #(.width(32)) register_2 (.D(Data_In_1), .en(Chip_Select), .Q(register_2_q), .clk(CLK), .clr(or_6_out));
  or or_6 (or_6_out, ~Chip_Select, Reset);  // OR_Gate
  Register #(.width(32)) register_3 (.D(Data_In_2), .en(Chip_Select), .Q(register_3_q), .clk(CLK), .clr(or_7_out));
  or or_7 (or_7_out, ~Chip_Select, Reset);  // OR_Gate
  Register #(.width(32)) register_4 (.D(Data_In_3), .en(Chip_Select), .Q(register_4_q), .clk(CLK), .clr(or_8_out));
  or or_8 (or_8_out, ~Chip_Select, Reset);  // OR_Gate
  Register #(.width(32)) register_5 (
    .D({{11{1'b1}}, nRead_Write, Mask, Address}), .en(Chip_Select), .Q(register_5_q), .clk(CLK),
    .clr(or_9_out));
  or or_9 (or_9_out, ~Chip_Select, Reset);  // OR_Gate
  D_Flip_Flop Proc (.clk(CLK), .D(or_4_out), .Q(Proc_q), .reset(or_10_out));  // open: Qn, preset, en
  or or_10 (or_10_out, ~Chip_Select, Reset);  // OR_Gate
  Demultiplexer #(.enable("false")) demultiplexer_2 (
    .out0(Count), .out1(Update_Mem), .in(demultiplexer_3_out0), .sel(Zero_Time));
  Demultiplexer #(.enable("false")) demultiplexer_3 (
    .out0(demultiplexer_3_out0), .out1(Load1), .in(Proc_q), .sel(Changed));
  Clock clock_1 (.out(CLK));
  Comparator #(.width(32)) comparator_2 (.a(register_1_q), .b(Data_In_0), .eq(comparator_2_eq));  // open: gt, lt
  Comparator #(.width(32)) comparator_3 (.a(register_2_q), .b(Data_In_1), .eq(comparator_3_eq));  // open: gt, lt
  Comparator #(.width(32)) comparator_4 (.a(register_3_q), .b(Data_In_2), .eq(comparator_4_eq));  // open: gt, lt
  Comparator #(.width(32)) comparator_5 (.a(register_4_q), .b(Data_In_3), .eq(comparator_5_eq));  // open: gt, lt
  Comparator #(.width(32)) comparator_6 (
    .a(register_5_q), .b({{11{1'b1}}, nRead_Write, Mask, Address}), .eq(comparator_6_eq));  // open: gt, lt
  nand nand_1 (nand_1_out, comparator_6_eq, comparator_2_eq, comparator_3_eq, comparator_4_eq, comparator_5_eq);
  and and_1 (Changed, nand_1_out, Chip_Select);
  or or_11 (Load, Count, Load1, Load0);
  and and_2 (and_2_out, Mask[0], Update_Mem, nRead_Write);
  and and_3 (and_3_out, Mask[1], Update_Mem, nRead_Write);
  and and_4 (and_4_out, Mask[2], Update_Mem, nRead_Write);
  and and_5 (and_5_out, Mask[3], Update_Mem, nRead_Write);
  RAM_part #(.addrWidth(16), .dataWidth(32), .bus("separate")) ram_1 (
    .addr(Address), .din(Data_In_0), .data(Data_Out_0), .str(and_2_out), .sel(Chip_Select), .clk(CLK),
    .ld(and_6_out), .clr(Reset));
  and and_6 (and_6_out, ~nRead_Write, Idle);  // AND_Gate
  RAM_part #(.addrWidth(16), .dataWidth(32), .bus("separate")) ram_2 (
    .addr(Address), .din(Data_In_1), .data(Data_Out_1), .str(and_3_out), .sel(Chip_Select), .clk(CLK),
    .ld(and_7_out), .clr(Reset));
  and and_7 (and_7_out, ~nRead_Write, Idle);  // AND_Gate
  RAM_part #(.addrWidth(16), .dataWidth(32), .bus("separate")) ram_3 (
    .addr(Address), .din(Data_In_2), .data(Data_Out_2), .str(and_4_out), .sel(Chip_Select), .clk(CLK),
    .ld(and_8_out), .clr(Reset));
  and and_8 (and_8_out, ~nRead_Write, Idle);  // AND_Gate
  RAM_part #(.addrWidth(16), .dataWidth(32), .bus("separate")) ram_4 (
    .addr(Address), .din(Data_In_3), .data(Data_Out_3), .str(and_5_out), .sel(Chip_Select), .clk(CLK),
    .ld(and_9_out), .clr(Reset));
  and and_9 (and_9_out, ~nRead_Write, Idle);  // AND_Gate

  assign Read_Time = 4'b0011;
  assign Write_Time = 4'b0010;

  // Other names for the same wires on the sheet: M0 = Mask[0]; M1 = Mask[1]; M2 = Mask[2]; M3 = Mask[3];
  //   RW = nRead_Write; CLR = Reset; CS = Chip_Select; Load2 = Count

  // Notes on the sheet:
  //   NO MODIFICAR
  //   excepto quizás los valores RT y WT
  //   BANK0
  //   BANK1
  //   BANK2
  //   BANK3
endmodule

module S_MIPS (
  input  Kbd_Available,
  input  [6:0] Kbd_ASCII_Data,
  input  [31:0] RAM_Out_0,
  input  [31:0] RAM_Out_1,
  input  Reset,
  input  [31:0] RAM_Out_2,
  input  Clock,
  input  [31:0] RAM_Out_3,
  input  [3:0] Read_Time,
  input  [3:0] Write_Time,
  output Kbd_Enable,
  output [15:0] Address,
  output Kbd_Clear,
  output TTY_Enable,
  output [6:0] TTY_ASCII_Data,
  output Stop,
  output [31:0] RAM_In_0,
  output [31:0] RAM_In_1,
  output [31:0] RAM_In_2,
  output [31:0] RAM_In_3,
  output [3:0] Mask,
  output nRead_Write,
  output Chip_Select
);


  // Other names for the same wires on the sheet: CLK = Clock; CLR = Reset; CS = Chip_Select;
  //   KBD_AVAIL = Kbd_Available; KBD_CLR = Kbd_Clear; KBD_DATA[6:0] = Kbd_ASCII_Data; RAM_A[15:0] = Address;
  //   RAM_INPUT_0[31:0] = RAM_In_0; RAM_INPUT_1[31:0] = RAM_In_1; RAM_INPUT_2[31:0] = RAM_In_2;
  //   RAM_INPUT_3[31:0] = RAM_In_3; RAM_MASK[3:0] = Mask; RAM_OUTPUT_0[31:0] = RAM_Out_0;
  //   RAM_OUTPUT_1[31:0] = RAM_Out_1; RAM_OUTPUT_2[31:0] = RAM_Out_2; RAM_OUTPUT_3[31:0] = RAM_Out_3;
  //   RW = nRead_Write; TTY_DATA[6:0] = TTY_ASCII_Data

  // Notes on the sheet:
  //   RAM ADDRESS
  //   DATA FROM RAM
  //   DATA TO RAM
  //   DATA WRITE MASK
  //   RAM TIMING
  //   RAM CONTROL
  //   KEYBOARD
  //   TTY
  //   SEQUENCING
endmodule

module RAM_Dispatcher (
  input  [3:0] WriteTime,
  input  Clock,
  input  CLR,
  output [31:0] Data,
  output [15:0] Address,
  output [3:0] Mask,
  output Finished,
  output Write
);

  wire demultiplexer_2_out1, demultiplexer_3_out1, End, IDLE_q, IncAddr, Load, or_1_out, or_2_out, While_q,
       WriteEnd;
  wire [3:0] counter_1_q;
  wire [31:0] CurrentAddress_q;

  Counter #(.width(32), .max('hffffffff)) CurrentAddress (
    .count(IncAddr), .Q({CurrentAddress_q[31:18], Address, CurrentAddress_q[1:0]}), .clk(Clock), .clr(CLR));  // open: load, D, carry
  or or_1 (or_1_out, IncAddr, demultiplexer_3_out1, Finished);
  D_Flip_Flop IDLE (.clk(Clock), .D(or_1_out), .Q(IDLE_q), .preset(CLR));  // open: Qn, en, reset
  Demultiplexer #(.enable("false")) demultiplexer_1 (.out0(Load), .out1(Finished), .in(IDLE_q), .sel(End));
  D_Flip_Flop While (.clk(Clock), .D(or_2_out), .Q(While_q), .reset(CLR));  // open: Qn, preset, en
  or or_2 (or_2_out, Write, Load);
  RAM_part #(.addrWidth(18), .dataWidth(32)) ram_1 (
    .addr({Address, CurrentAddress_q[1:0]}), .data(Data), .clk(Clock));  // open: sel, ld, clr
  Demultiplexer #(.enable("false")) demultiplexer_2 (
    .out0(Write), .out1(demultiplexer_2_out1), .in(While_q), .sel(WriteEnd));
  Decoder #(.select(2)) decoder_1 (
    .out0(Mask[0]), .out1(Mask[1]), .out2(Mask[2]), .out3(Mask[3]), .sel(CurrentAddress_q[1:0]));  // open: en
  Demultiplexer #(.enable("false")) demultiplexer_3 (
    .out0(IncAddr), .out1(demultiplexer_3_out1), .in(demultiplexer_2_out1), .sel(End));
  Counter #(.width(4), .max('hf)) counter_1 (
    .load(Load), .D(WriteTime), .count(Write), .Q(counter_1_q), .clk(Clock));  // open: carry, clr
  Comparator #(.width(32)) comparator_1 (.a(Data), .b({32{1'b1}}), .eq(End));  // open: gt, lt
  Comparator #(.width(4)) comparator_2 (.a(4'b0000), .b(counter_1_q), .eq(WriteEnd));  // open: gt, lt

  // Other names for the same wires on the sheet: CLK = Clock; Count = Write; WT[3:0] = WriteTime
endmodule

module ALU (
  input  [31:0] in_1,
  input  Overflow,
  input  [31:0] in_3,
  input  Zero,
  input  Neg,
  input  [2:0] in_6,
  output [31:0] Output
);

  wire [31:0] ResultAnd, ResultDiv, ResultMult, ResultNeg, ResultOr, ResultSub, ResultSum, ResultXor,
       undriven, undriven_2, undriven_3, undriven_4, undriven_5, undriven_6;

  Adder #(.width(32)) adder_1 (.a(in_1), .b(in_3), .out(ResultSum), .cout(Overflow));  // open: cin
  Multiplier #(.width(32)) multiplier_1 (.a(in_1), .b(in_3), .out(ResultMult));  // open: cin, cout
  assign ResultAnd = in_1 & in_3;  // AND_Gate and_1, 32 bits wide
  Subtractor #(.width(32)) subtractor_1 (.a(in_1), .b(in_3), .out(ResultSub), .bout(Neg));  // open: bin
  Divider #(.width(32)) divider_1 (.a(in_1), .b(in_3), .out(ResultDiv));  // open: upper, rem
  Multiplexer #(.select(3), .width(32)) multiplexer_1 (
    .in0(undriven), .in1(undriven_2), .in2(undriven_3), .in3(ResultMult), .in4(undriven_5), .in5(undriven_6),
    .in6(undriven_4), .out(Output), .sel(in_6));  // open: in7, en
  assign ResultOr = in_1 | in_3;  // OR_Gate or_1, 32 bits wide
  Negator #(.width(32)) negator_1 (.in(in_1), .out(ResultNeg));
  Comparator #(.width(32)) comparator_1 (.a(in_1), .b(in_3), .eq(Zero), .lt(Neg));  // open: gt
  assign ResultXor = in_1 ^ in_3;  // XOR_Gate xor_1, 32 bits wide

  // Other names for the same wires on the sheet: a[31:0] = in_1; b[31:0] = in_3; Result[31:0] = Output
endmodule

module Prueba (
  input  [31:0] in_1,
  input  [2:0] in_2,
  input  [31:0] in_3,
  output [31:0] Output,
  output Output_2,
  output Output_3,
  output Output_4
);

  // Probe on in_1
  // Probe on in_3
  RF rf_1 ();  // open: Selector, Input, RW, Output_A, Output_B, Selector_A, Selector_B
  ALU alu_1 (
    .in_1(in_1), .in_3(in_3), .in_6(in_2), .Output(Output), .Overflow(Output_2), .Zero(Output_3),
    .Neg(Output_4));
  // Probe on Output
endmodule

module RF (
  input  [4:0] Selector,
  input  [31:0] Input,
  input  RW,
  input  [4:0] Selector_B,
  input  [4:0] Selector_A,
  output [31:0] Output_A,
  output [31:0] Output_B
);

  wire e0, e1, e2, e3, e4, e5, e6, e7, e8, e9, e10, e11, e12, e13, e14, e15, e16, e17, e18, e19, e20, e21,
       e22, e23, e24, e25, e26, e27, e28, e29, e30, e31;
  wire [31:0] o1, o2, o3, o4, o5, o6, o7, o8, o9, o10, o11, o12, o13, o14, o15, o16, o17, o18, o19, o20, o21,
       o22, o23, o24, o25, o26, o27, o28, o29, o30, o31;

  Register #(.width(32)) r1 (.D(Input), .en(e1), .Q(o1));  // open: clk, clr
  Register #(.width(32)) r8 (.D(Input), .en(e8), .Q(o8));  // open: clk, clr
  Register #(.width(32)) r15 (.D(Input), .en(e15), .Q(o15));  // open: clk, clr
  Register #(.width(32)) r22 (.D(Input), .en(e22), .Q(o22));  // open: clk, clr
  Register #(.width(32)) r29 (.D(Input), .en(e29), .Q(o29));  // open: clk, clr
  Register #(.width(32)) r2 (.D(Input), .en(e2), .Q(o2));  // open: clk, clr
  Register #(.width(32)) r9 (.D(Input), .en(e9), .Q(o9));  // open: clk, clr
  Register #(.width(32)) r16 (.D(Input), .en(e16), .Q(o16));  // open: clk, clr
  Register #(.width(32)) r23 (.D(Input), .en(e23), .Q(o23));  // open: clk, clr
  Register #(.width(32)) r30 (.D(Input), .en(e30), .Q(o30));  // open: clk, clr
  Register #(.width(32)) r3 (.D(Input), .en(e3), .Q(o3));  // open: clk, clr
  Register #(.width(32)) r10 (.D(Input), .en(e10), .Q(o10));  // open: clk, clr
  Register #(.width(32)) r17 (.D(Input), .en(e17), .Q(o17));  // open: clk, clr
  Register #(.width(32)) r24 (.D(Input), .en(e24), .Q(o24));  // open: clk, clr
  Register #(.width(32)) r31 (.D(Input), .en(e31), .Q(o31));  // open: clk, clr
  Register #(.width(32)) r4 (.D(Input), .en(e4), .Q(o4));  // open: clk, clr
  Register #(.width(32)) r11 (.D(Input), .en(e11), .Q(o11));  // open: clk, clr
  Register #(.width(32)) r18 (.D(Input), .en(e18), .Q(o18));  // open: clk, clr
  Register #(.width(32)) r25 (.D(Input), .en(e25), .Q(o25));  // open: clk, clr
  Decoder #(.select(5)) decoder_1 (
    .out0(e0), .out1(e1), .out2(e2), .out3(e3), .out4(e4), .out5(e5), .out6(e6), .out7(e7), .out8(e8),
    .out9(e9), .out10(e10), .out11(e11), .out12(e12), .out13(e13), .out14(e14), .out15(e15), .out16(e16),
    .out17(e17), .out18(e18), .out19(e19), .out20(e20), .out21(e21), .out22(e22), .out23(e23), .out24(e24),
    .out25(e25), .out26(e26), .out27(e27), .out28(e28), .out29(e29), .out30(e30), .out31(e31),
    .sel(Selector), .en(RW));
  Register #(.width(32)) r5 (.D(Input), .en(e5), .Q(o5));  // open: clk, clr
  Register #(.width(32)) r12 (.D(Input), .en(e12), .Q(o12));  // open: clk, clr
  Register #(.width(32)) r19 (.D(Input), .en(e19), .Q(o19));  // open: clk, clr
  Register #(.width(32)) r26 (.D(Input), .en(e26), .Q(o26));  // open: clk, clr
  Register #(.width(32)) r6 (.D(Input), .en(e6), .Q(o6));  // open: clk, clr
  Register #(.width(32)) r13 (.D(Input), .en(e13), .Q(o13));  // open: clk, clr
  Register #(.width(32)) r20 (.D(Input), .en(e20), .Q(o20));  // open: clk, clr
  Register #(.width(32)) r27 (.D(Input), .en(e27), .Q(o27));  // open: clk, clr
  Register #(.width(32)) r7 (.D(Input), .en(e7), .Q(o7));  // open: clk, clr
  Register #(.width(32)) r14 (.D(Input), .en(e14), .Q(o14));  // open: clk, clr
  Register #(.width(32)) r21 (.D(Input), .en(e21), .Q(o21));  // open: clk, clr
  Register #(.width(32)) r28 (.D(Input), .en(e28), .Q(o28));  // open: clk, clr
  Multiplexer #(.select(5), .width(32), .enable("false")) multiplexer_1 (
    .in0({32{1'b0}}), .in1(o1), .in2(o2), .in3(o3), .in4(o4), .in5(o5), .in6(o6), .in7(o7), .in8(o8),
    .in9(o9), .in10(o10), .in11(o11), .in12(o12), .in13(o13), .in14(o14), .in15(o15), .in16(o16), .in17(o17),
    .in18(o18), .in19(o19), .in20(o20), .in21(o21), .in22(o22), .in23(o23), .in24(o24), .in25(o25),
    .in26(o26), .in27(o27), .in28(o28), .in29(o29), .in30(o30), .in31(o31), .out(Output_A));  // open: sel
  Multiplexer #(.select(5), .width(32), .enable("false")) multiplexer_2 (
    .in0({32{1'b0}}), .in1(o1), .in2(o2), .in3(o3), .in4(o4), .in5(o5), .in6(o6), .in7(o7), .in8(o8),
    .in9(o9), .in10(o10), .in11(o11), .in12(o12), .in13(o13), .in14(o14), .in15(o15), .in16(o16), .in17(o17),
    .in18(o18), .in19(o19), .in20(o20), .in21(o21), .in22(o22), .in23(o23), .in24(o24), .in25(o25),
    .in26(o26), .in27(o27), .in28(o28), .in29(o29), .in30(o30), .in31(o31), .out(Output_B));  // open: sel
endmodule

module ID (
  input  [31:0] Input,
  output [5:0] Op_Code,
  output [4:0] Rs,
  output [4:0] Rt,
  output [4:0] Rd,
  output [4:0] x,
  output [5:0] Func_code,
  output [15:0] constante,
  output [25:0] Destino
);


  assign constante = Input[31:16];
  assign Destino = Input[31:6];
  assign Func_code = Input[31:26];
  assign Op_Code = Input[5:0];
  assign Rd = Input[20:16];
  assign Rs = Input[10:6];
  assign Rt = Input[15:11];
  assign x = Input[25:21];
endmodule

module mul_mulu (
  input  [31:0] in_1,
  input  in_2,
  input  [31:0] in_3,
  output [31:0] out_lo,
  output [31:0] out_hi
);

  wire _1er_bit_de_lo, neg_a, neg_b, neg_lo;
  wire [30:0] lo;
  wire [31:0] negator_1_out, negator_2_out, negator_3_out, result_a, result_b;

  Negator #(.width(32)) negator_1 (.in(in_1), .out(negator_1_out));
  // Probe on in_1
  // Probe on in_3
  and and_1 (neg_a, in_1[31], in_2);
  Multiplexer #(.width(32)) multiplexer_1 (.in0(in_1), .in1(negator_1_out), .out(result_a), .sel(neg_a));  // open: en
  and and_2 (neg_b, in_3[31], in_2);
  Multiplexer #(.width(32)) multiplexer_2 (.in0(in_3), .in1(negator_2_out), .out(result_b), .sel(neg_b));  // open: en
  Negator #(.width(32)) negator_2 (.in(in_3), .out(negator_2_out));
  Multiplier #(.width(32)) multiplier_1 (
    .a(result_a), .b(result_b), .out({_1er_bit_de_lo, lo}), .cout(out_hi));  // open: cin
  and and_3 (neg_lo, _1er_bit_de_lo, in_2);
  Multiplexer #(.width(32)) multiplexer_3 (
    .in0({_1er_bit_de_lo, lo}), .in1(negator_3_out), .out(out_lo), .sel(neg_lo));  // open: en
  Negator #(.width(32)) negator_3 (.in({_1er_bit_de_lo, lo}), .out(negator_3_out));
  // Probe on out_lo

  // Other names for the same wires on the sheet: a[31:0] = in_1; _1er_bit_de_a = in_1[31]; b[31:0] = in_3;
  //   _1er_bit_de_b = in_3[31]; con_signo = in_2; hi[31:0] = out_hi; lo[31] = _1er_bit_de_lo;
  //   result_lo[31:0] = out_lo
endmodule

module div_divu (
  input  [31:0] in_1,
  input  in_2,
  input  [31:0] in_3,
  output [31:0] out_lo,
  output [31:0] out_hi
);

  wire _1er_bit_de_lo, neg_a, neg_b, neg_lo;
  wire [30:0] lo;
  wire [31:0] negator_1_out, negator_2_out, negator_3_out, result_a, result_b;

  Negator #(.width(32)) negator_1 (.in(in_1), .out(negator_1_out));
  and and_1 (neg_a, in_1[31], in_2);
  Multiplexer #(.width(32)) multiplexer_1 (.in0(in_1), .in1(negator_1_out), .out(result_a), .sel(neg_a));  // open: en
  and and_2 (neg_b, in_3[31], in_2);
  Multiplexer #(.width(32)) multiplexer_2 (.in0(in_3), .in1(negator_2_out), .out(result_b), .sel(neg_b));  // open: en
  Negator #(.width(32)) negator_2 (.in(in_3), .out(negator_2_out));
  Divider #(.width(32)) divider_1 (
    .a(result_a), .b(result_b), .out({_1er_bit_de_lo, lo}), .rem(out_hi));  // open: upper
  and and_3 (neg_lo, _1er_bit_de_lo, in_2);
  Multiplexer #(.width(32)) multiplexer_3 (
    .in0({_1er_bit_de_lo, lo}), .in1(negator_3_out), .out(out_lo), .sel(neg_lo));  // open: en
  Negator #(.width(32)) negator_3 (.in({_1er_bit_de_lo, lo}), .out(negator_3_out));

  // Other names for the same wires on the sheet: a[31:0] = in_1; _1er_bit_de_a = in_1[31]; b[31:0] = in_3;
  //   _1er_bit_de_b = in_3[31]; con_signo = in_2; hi[31:0] = out_hi; lo[31] = _1er_bit_de_lo;
  //   result_lo[31:0] = out_lo
endmodule

module slt_sltu (
  input  [31:0] in_1,
  input  in_2,
  input  [31:0] in_3,
  output [31:0] out
);

  wire comparator_1_lt, neg_a, neg_b;
  wire [31:0] negator_1_out, negator_2_out, result_a, result_b;

  Negator #(.width(32)) negator_1 (.in(in_1), .out(negator_1_out));
  and and_1 (neg_a, in_1[31], in_2);
  Multiplexer #(.width(32)) multiplexer_1 (.in0(in_1), .in1(negator_1_out), .out(result_a), .sel(neg_a));  // open: en
  and and_2 (neg_b, in_3[31], in_2);
  Multiplexer #(.width(32)) multiplexer_2 (.in0(in_3), .in1(negator_2_out), .out(result_b), .sel(neg_b));  // open: en
  Negator #(.width(32)) negator_2 (.in(in_3), .out(negator_2_out));
  Comparator #(.width(32)) comparator_1 (.a(result_a), .b(result_b), .lt(comparator_1_lt));  // open: gt, eq
  Multiplexer #(.width(32)) multiplexer_3 (
    .in0({32{1'b0}}), .in1(32'h1), .out(out), .sel(comparator_1_lt));  // open: en

  // Other names for the same wires on the sheet: a[31:0] = in_1; _1er_bit_de_a = in_1[31]; b[31:0] = in_3;
  //   _1er_bit_de_b = in_3[31]; con_signo = in_2; result[31:0] = out
endmodule

module andi_ori_xori (
  input  [1:0] in_1,
  input  [31:0] in_2,
  input  [15:0] in_3,
  output [31:0] out
);

  wire [31:0] andi, ori, xori;

  assign andi = in_2 & {{16{1'b0}}, in_3};  // AND_Gate and_1, 32 bits wide
  assign ori = in_2 | {{16{1'b0}}, in_3};  // OR_Gate or_1, 32 bits wide
  assign xori = in_2 ^ {{16{1'b0}}, in_3};  // XOR_Gate xor_1, 32 bits wide
  Multiplexer #(.select(2), .width(32)) multiplexer_1 (
    .in0(andi), .in1(ori), .in2(xori), .out(out), .sel(in_1));  // open: in3, en

  // Other names for the same wires on the sheet: a[31:0] = in_2; b[15:0] = in_3; constante[15:0] = in_3;
  //   result[31:0] = out; selector[1:0] = in_1
endmodule

module slti_sltiu (
  input  [31:0] in_1,
  input  in_2,
  input  [15:0] in_3,
  output [31:0] out
);

  wire comparator_1_lt, neg_a, neg_b;
  wire [31:0] negator_1_out, negator_2_out, result_a, result_b;

  Negator #(.width(32)) negator_1 (.in(in_1), .out(negator_1_out));
  and and_1 (neg_a, in_1[31], in_2);
  Multiplexer #(.width(32)) multiplexer_1 (.in0(in_1), .in1(negator_1_out), .out(result_a), .sel(neg_a));  // open: en
  and and_2 (neg_b, in_3[15], in_2);
  Multiplexer #(.width(32)) multiplexer_2 (
    .in0({{17{in_3[15]}}, in_3[14:0]}), .in1(negator_2_out), .out(result_b), .sel(neg_b));  // open: en
  Negator #(.width(32)) negator_2 (.in({{17{in_3[15]}}, in_3[14:0]}), .out(negator_2_out));
  Comparator #(.width(32)) comparator_1 (.a(result_a), .b(result_b), .lt(comparator_1_lt));  // open: gt, eq
  Multiplexer #(.width(32)) multiplexer_3 (
    .in0({32{1'b0}}), .in1(32'h1), .out(out), .sel(comparator_1_lt));  // open: en

  // Other names for the same wires on the sheet: a[31:0] = in_1; _1er_bit_de_a = in_1[31];
  //   b[31:0] = {{17{in_3[15]}}, in_3[14:0]}; constante[15:0] = in_3; _1er_bit_de_b = in_3[15]; con_signo = in_2;
  //   result[31:0] = out
endmodule

module addi (
  input  [31:0] in_1,
  input  [15:0] in_2,
  output [31:0] out
);

  Adder #(.width(32)) adder_1 (.a(in_1), .b({{17{in_2[15]}}, in_2[14:0]}), .out(out));  // open: cin, cout

  // Other names for the same wires on the sheet: a[31:0] = in_1; b[31:0] = {{17{in_2[15]}}, in_2[14:0]};
  //   constante[15:0] = in_2; result[31:0] = out
endmodule

module lw (
  input  [31:0] in_1,
  input  [15:0] in_2,
  output [31:0] direccion
);

  wire [31:0] divider_1_rem, result_a;

  Divider #(.width(32)) divider_1 (.a(result_a), .b(32'h4), .rem(divider_1_rem));  // open: out, upper
  andi_ori_xori andi_ori_xori_1 (.in_2(in_1), .in_3(in_2), .out(result_a), .in_1(2'b00));
  Subtractor #(.width(32)) subtractor_1 (.a(result_a), .b(divider_1_rem), .out(direccion));  // open: bin, bout

  // Other names for the same wires on the sheet: a[31:0] = in_1; constante[15:0] = in_2
endmodule
